# Fritzing sketch schema (saved by Fritzing 0.9.2b)
breadboards: 1

parts:
  R1 = Resistor [tolerance=±5% resistance=220 package=THT]
  R2 = Resistor [tolerance=±5% resistance=4.7k package=THT]
  part = Arduino Nano (Rev3.0)
  LED1 = LED - 5mm [color="Red (633nm)" package="5 mm [THT]"]
  DS1 = DS18B20 1-Wire Temperature Sensor [part_number=DS18B20]
  IC1 = DIP - 20 pins [chip_label="Dragino LoRa BEE v1.1" package="DIP (Dual Inline) [THT]"]

nets:
  N1: R1.Pin_0, LED1.cathode
  GND: R1.Pin_1, part.GND, DS1.GND, IC1.GND
  5V: R2.Pin_0, part.5V, DS1.VDD
  N2: R2.Pin_1, part.D4, DS1.DQ
  N3: part.D2, IC1.DIO0
  N4: part.D5, LED1.anode
  N5: part.D9, IC1.RESET
  N6: part.D10, IC1.NSS
  N7: part.D11/MOSI, IC1.MOSI
  N8: part.D12/MISO, IC1.MISO
  3V3: part.3V3, IC1.3V3
  N9: part.D13/SCK, IC1.SCK

custom parts:
  DIP - 20 pins: A DIP stand-in part for whatever IC you want. With 20 pins on a 600mil dual inline package (DIP) footprint.
